// Logisim project 4bitALU.circ as structural Verilog: 2 circuits, main circuit alu
module alu (
  input  [3:0] A,
  input  [3:0] B,
  input  [1:0] ALUOp,
  output [3:0] C
);

  wire [3:0] ADD, AND, OR, SUB;

  Multiplexer #(.select(2), .width(4)) multiplexer_1 (
    .in0(ADD), .in1(SUB), .in2(AND), .in3(OR), .out(C), .sel(ALUOp));  // open: en
  Adder #(.width(4)) adder_1 (.a(A), .b(B), .out(ADD));  // open: cin, cout
  Subtractor #(.width(4)) subtractor_1 (.a(A), .b(B), .out(SUB));  // open: bin, bout
  assign AND = A & B;  // AND_Gate and_1, 4 bits wide
  assign OR = A | B;  // OR_Gate or_1, 4 bits wide

  // Other names for the same wires on the sheet: Op[1:0] = ALUOp
endmodule

module test (
  output [3:0] out_1
);

  wire clock_1_out, clock_2_out;
  wire [1:0] counter_2_q;
  wire [7:0] counter_1_q, rom_1_data;

  Clock clock_1 (.out(clock_1_out));
  Counter counter_1 (.Q(counter_1_q), .clk(clock_1_out));  // open: load, D, count, carry, clr
  ROM rom_1 (.addr(counter_1_q), .data(rom_1_data));  // open: sel
  Counter #(.width(2), .max('h3)) counter_2 (.Q(counter_2_q), .clk(clock_2_out));  // open: load, D, count, carry, clr
  Clock clock_2 (.out(clock_2_out));
  alu alu_1 (.A(rom_1_data[3:0]), .B(rom_1_data[7:4]), .ALUOp(counter_2_q), .C(out_1));
endmodule
