// Logisim project CRC.circ as structural Verilog: 3 circuits, main circuit CRC
module CRC (
  input  [7:0] in_1,
  input  [3:0] in_2,
  output [10:0] out_3
);

  wire [2:0] div_1_out_3, div_2_out_3, div_3_out_3, div_4_out_3, div_5_out_3, div_6_out_3;
  wire [3:1] div_7_out_3;

  div div_1 (.A(in_1[7:4]), .B(in_2), .out_3(div_1_out_3));
  // Probe on div_1_out_3
  div div_2 (.A({div_1_out_3, in_1[3]}), .B(in_2), .out_3(div_2_out_3));
  // Probe on div_2_out_3
  div div_3 (.A({div_2_out_3, in_1[2]}), .B(in_2), .out_3(div_3_out_3));
  // Probe on div_3_out_3
  div div_4 (.A({div_3_out_3, in_1[1]}), .B(in_2), .out_3(div_4_out_3));
  div div_5 (.A({div_4_out_3, in_1[0]}), .B(in_2), .out_3(div_5_out_3));
  div div_6 (.A({div_5_out_3, 1'b0}), .B(in_2), .out_3(div_6_out_3));
  div div_7 (.A({div_6_out_3, 1'b0}), .B(in_2), .out_3(div_7_out_3));
  div div_8 (.A({div_7_out_3, 1'b0}), .B(in_2), .out_3(out_3[2:0]));

  assign out_3[10:3] = in_1;

  // Other names for the same wires on the sheet: A[7:0] = in_1; AO[10:3] = in_1; B[3:0] = in_2; rem[2:0] = out_3[2:0]
endmodule

module div (
  input  [3:0] A,
  input  [3:0] B,
  output [2:0] out_3
);

  wire [3:0] xor_1_out;

  assign xor_1_out = A ^ B;  // XOR_Gate xor_1, 4 bits wide
  Multiplexer #(.width(3)) multiplexer_1 (.in0(A[2:0]), .in1(xor_1_out[2:0]), .out(out_3), .sel(A[3]));  // open: en
endmodule

module test (
  output [10:0] out_1
);

  wire clock_1_out;
  wire [7:0] counter_1_q;
  wire [11:0] rom_1_data;

  Counter counter_1 (.Q(counter_1_q), .clk(clock_1_out));  // open: load, D, count, carry, clr
  Clock clock_1 (.out(clock_1_out));
  ROM #(.dataWidth(12)) rom_1 (.addr(counter_1_q), .data(rom_1_data));  // open: sel
  CRC crc_1 (.in_1(rom_1_data[7:0]), .in_2(rom_1_data[11:8]), .out_3(out_1));
endmodule
