// Logisim project GRF.circ as structural Verilog: 8 circuits, main circuit single_reg
module single_reg (
  input  [31:0] in_1,
  input  clk,
  input  en,
  input  reset,
  output [31:0] out_5
);

  wire [31:0] multiplexer_1_out, multiplexer_2_out;

  Multiplexer #(.width(32)) multiplexer_1 (.in0(out_5), .in1(in_1), .out(multiplexer_1_out), .sel(en));  // open: en
  Multiplexer #(.width(32)) multiplexer_2 (
    .in0(multiplexer_1_out), .in1({32{1'b0}}), .out(multiplexer_2_out), .sel(reset));  // open: en
  Register #(.width(32)) register_1 (.D(multiplexer_2_out), .en(1'b1), .Q(out_5), .clk(clk), .clr(reset));
endmodule

module _2_reg (
  input  A1,
  input  clk,
  input  reset,
  input  WE,
  input  A2,
  input  A3,
  input  [31:0] WD,
  output [31:0] RD1,
  output [31:0] RD2
);

  wire not_1_out, WE0, WE1;
  wire [31:0] single_reg_1_out_5, single_reg_2_out_5;

  not not_1 (not_1_out, A3);
  and and_1 (WE0, WE, not_1_out);
  and and_2 (WE1, WE, A3);
  single_reg single_reg_1 (.in_1(WD), .clk(clk), .en(WE0), .reset(reset), .out_5(single_reg_1_out_5));
  single_reg single_reg_2 (.in_1(WD), .clk(clk), .en(WE1), .reset(reset), .out_5(single_reg_2_out_5));
  Multiplexer #(.width(32)) multiplexer_1 (
    .in0(single_reg_1_out_5), .in1(single_reg_2_out_5), .out(RD1), .sel(A1));  // open: en
  Multiplexer #(.width(32)) multiplexer_2 (
    .in0(single_reg_1_out_5), .in1(single_reg_2_out_5), .out(RD2), .sel(A2));  // open: en
endmodule

module _4_reg (
  input  clk,
  input  reset,
  input  WE,
  input  [1:0] A1,
  input  [1:0] A2,
  input  [1:0] A3,
  input  [31:0] WD,
  output [31:0] RD1,
  output [31:0] RD2
);

  wire not_1_out, WE0, WE1;
  wire [31:0] n2_reg_1_rd1, n2_reg_1_rd2, n2_reg_2_rd1, n2_reg_2_rd2;

  not not_1 (not_1_out, A3[1]);
  and and_1 (WE0, WE, not_1_out);
  and and_2 (WE1, WE, A3[1]);
  _2_reg u_2_reg_1 (
    .A1(A1[0]), .A2(A2[0]), .A3(A3[0]), .WD(WD), .clk(clk), .reset(reset), .WE(WE0), .RD1(n2_reg_1_rd1),
    .RD2(n2_reg_1_rd2));
  _2_reg u_2_reg_2 (
    .A1(A1[0]), .A2(A2[0]), .A3(A3[0]), .WD(WD), .clk(clk), .reset(reset), .WE(WE1), .RD1(n2_reg_2_rd1),
    .RD2(n2_reg_2_rd2));
  Multiplexer #(.width(32)) multiplexer_1 (.in0(n2_reg_1_rd1), .in1(n2_reg_2_rd1), .out(RD1), .sel(A1[1]));  // open: en
  Multiplexer #(.width(32)) multiplexer_2 (.in0(n2_reg_1_rd2), .in1(n2_reg_2_rd2), .out(RD2), .sel(A2[1]));  // open: en

  // Other names for the same wires on the sheet: A1_next = A1[0]; A1_now = A1[1]; A2_next = A2[0]; A2_now = A2[1];
  //   A3_next = A3[0]; A3_now = A3[1]
endmodule

module _8_reg (
  input  clk,
  input  reset,
  input  WE,
  input  [2:0] A1,
  input  [2:0] A2,
  input  [2:0] A3,
  input  [31:0] WD,
  output [31:0] RD1,
  output [31:0] RD2
);

  wire not_1_out, WE0, WE1;
  wire [31:0] n4_reg_1_rd1, n4_reg_1_rd2, n4_reg_2_rd1, n4_reg_2_rd2;

  not not_1 (not_1_out, A3[2]);
  and and_1 (WE0, WE, not_1_out);
  and and_2 (WE1, WE, A3[2]);
  _4_reg u_4_reg_1 (
    .A1(A1[1:0]), .A2(A2[1:0]), .A3(A3[1:0]), .WD(WD), .clk(clk), .reset(reset), .WE(WE0),
    .RD1(n4_reg_1_rd1), .RD2(n4_reg_1_rd2));
  _4_reg u_4_reg_2 (
    .A1(A1[1:0]), .A2(A2[1:0]), .A3(A3[1:0]), .WD(WD), .clk(clk), .reset(reset), .WE(WE1),
    .RD1(n4_reg_2_rd1), .RD2(n4_reg_2_rd2));
  Multiplexer #(.width(32)) multiplexer_1 (.in0(n4_reg_1_rd1), .in1(n4_reg_2_rd1), .out(RD1), .sel(A1[2]));  // open: en
  Multiplexer #(.width(32)) multiplexer_2 (.in0(n4_reg_1_rd2), .in1(n4_reg_2_rd2), .out(RD2), .sel(A2[2]));  // open: en

  // Other names for the same wires on the sheet: A1_next[1:0] = A1[1:0]; A1_now = A1[2]; A2_next[1:0] = A2[1:0];
  //   A2_now = A2[2]; A3_next[1:0] = A3[1:0]; A3_now = A3[2]
endmodule

module _16_reg (
  input  clk,
  input  reset,
  input  WE,
  input  [3:0] A1,
  input  [3:0] A2,
  input  [3:0] A3,
  input  [31:0] WD,
  output [31:0] RD1,
  output [31:0] RD2
);

  wire not_1_out, WE0, WE1;
  wire [31:0] n8_reg_1_rd1, n8_reg_1_rd2, n8_reg_2_rd1, n8_reg_2_rd2;

  not not_1 (not_1_out, A3[3]);
  and and_1 (WE0, WE, not_1_out);
  and and_2 (WE1, WE, A3[3]);
  _8_reg u_8_reg_1 (
    .A1(A1[2:0]), .A2(A2[2:0]), .A3(A3[2:0]), .WD(WD), .clk(clk), .reset(reset), .WE(WE0),
    .RD1(n8_reg_1_rd1), .RD2(n8_reg_1_rd2));
  _8_reg u_8_reg_2 (
    .A1(A1[2:0]), .A2(A2[2:0]), .A3(A3[2:0]), .WD(WD), .clk(clk), .reset(reset), .WE(WE1),
    .RD1(n8_reg_2_rd1), .RD2(n8_reg_2_rd2));
  Multiplexer #(.width(32)) multiplexer_1 (.in0(n8_reg_1_rd1), .in1(n8_reg_2_rd1), .out(RD1), .sel(A1[3]));  // open: en
  Multiplexer #(.width(32)) multiplexer_2 (.in0(n8_reg_1_rd2), .in1(n8_reg_2_rd2), .out(RD2), .sel(A2[3]));  // open: en

  // Other names for the same wires on the sheet: A1_next[2:0] = A1[2:0]; A1_now = A1[3]; A2_next[2:0] = A2[2:0];
  //   A2_now = A2[3]; A3_next[2:0] = A3[2:0]; A3_now = A3[3]
endmodule

module _32_reg (
  input  clk,
  input  reset,
  input  WE,
  input  [4:0] A1,
  input  [4:0] A2,
  input  [4:0] A3,
  input  [31:0] WD,
  output [31:0] RD1,
  output [31:0] RD2
);

  wire not_1_out, WE0, WE1;
  wire [31:0] n16_reg_1_rd1, n16_reg_1_rd2, n16_reg_2_rd1, n16_reg_2_rd2;

  not not_1 (not_1_out, A3[4]);
  and and_1 (WE0, WE, not_1_out);
  and and_2 (WE1, WE, A3[4]);
  _16_reg u_16_reg_1 (
    .A1(A1[3:0]), .A2(A2[3:0]), .A3(A3[3:0]), .WD(WD), .clk(clk), .reset(reset), .WE(WE0),
    .RD1(n16_reg_1_rd1), .RD2(n16_reg_1_rd2));
  _16_reg u_16_reg_2 (
    .A1(A1[3:0]), .A2(A2[3:0]), .A3(A3[3:0]), .WD(WD), .clk(clk), .reset(reset), .WE(WE1),
    .RD1(n16_reg_2_rd1), .RD2(n16_reg_2_rd2));
  Multiplexer #(.width(32)) multiplexer_1 (
    .in0(n16_reg_1_rd1), .in1(n16_reg_2_rd1), .out(RD1), .sel(A1[4]));  // open: en
  Multiplexer #(.width(32)) multiplexer_2 (
    .in0(n16_reg_1_rd2), .in1(n16_reg_2_rd2), .out(RD2), .sel(A2[4]));  // open: en

  // Other names for the same wires on the sheet: A1_next[3:0] = A1[3:0]; A1_now = A1[4]; A2_next[3:0] = A2[3:0];
  //   A2_now = A2[4]; A3_next[3:0] = A3[3:0]; A3_now = A3[4]
endmodule

module grf (
  input  clk,
  input  reset,
  input  WE,
  input  [4:0] A1,
  input  [4:0] A2,
  input  [4:0] A3,
  input  [31:0] WD,
  output [31:0] RD1,
  output [31:0] RD2
);

  wire comparator_1_eq;
  wire [31:0] multiplexer_1_out;

  Comparator #(.width(5), .mode("unsigned")) comparator_1 (
    .a(A3), .b({5{1'b0}}), .eq(comparator_1_eq));  // open: gt, lt
  Multiplexer #(.width(32)) multiplexer_1 (
    .in0(WD), .in1({32{1'b0}}), .out(multiplexer_1_out), .sel(comparator_1_eq));  // open: en
  _32_reg u_32_reg_1 (
    .A1(A1), .A2(A2), .A3(A3), .WD(multiplexer_1_out), .clk(clk), .reset(reset), .WE(WE), .RD1(RD1), .RD2(RD2));
endmodule

module test (
  output [31:0] RD1,
  output [31:0] RD2
);

  wire clock_1_out;
  wire [7:0] counter_1_q;
  wire [16:0] rom_1_data;
  wire [31:0] rom_2_data;

  Counter counter_1 (.Q(counter_1_q), .clk(clock_1_out));  // open: load, D, count, carry, clr
  Clock clock_1 (.out(clock_1_out));
  ROM #(.dataWidth(17)) rom_1 (.addr(counter_1_q), .data(rom_1_data));  // open: sel
  ROM #(.dataWidth(32)) rom_2 (.addr(counter_1_q), .data(rom_2_data));  // open: sel
  _32_reg u_32_reg_1 (
    .A1(rom_1_data[6:2]), .A2(rom_1_data[11:7]), .A3(rom_1_data[16:12]), .WD(rom_2_data), .clk(clock_1_out),
    .reset(rom_1_data[1]), .WE(rom_1_data[0]), .RD1(RD1), .RD2(RD2));
endmodule
