// Logisim project fsm.circ as structural Verilog: 6 circuits, main circuit fsm
module fsm (
  input  CLR,
  input  [1:0] In,
  output Z
);

  wire clock_1_out;
  wire [2:0] reg_1_q, trans_1_next;

  Clock clock_1 (.out(clock_1_out));
  trans trans_1 (.state(reg_1_q), .In(In), .next(trans_1_next));
  \reg  reg_1 (.D(trans_1_next), .CLK(clock_1_out), .CLR(CLR), .Q(reg_1_q));
  out out_1 (.In(In), .state(reg_1_q), .Z(Z));
endmodule

module trans (
  input  [2:0] state,
  input  [1:0] In,
  output [2:0] next
);

  wire comb_1_ss0, comb_1_ss1, comb_1_ss2, comb_1_ss3, comb_1_ss4, decoder_1_out0, decoder_1_out1,
       decoder_1_out2, decoder_1_out3, decoder_1_out4;

  Decoder #(.select(3)) decoder_1 (
    .out0(decoder_1_out0), .out1(decoder_1_out1), .out2(decoder_1_out2), .out3(decoder_1_out3),
    .out4(decoder_1_out4), .sel(state));  // open: out5, out6, out7, en
  comb comb_1 (
    .S0(decoder_1_out0), .S1(decoder_1_out1), .S2(decoder_1_out2), .S3(decoder_1_out3), .S4(decoder_1_out4),
    .I1(In[1]), .I2(In[0]), .SS0(comb_1_ss0), .SS1(comb_1_ss1), .SS2(comb_1_ss2), .SS3(comb_1_ss3),
    .SS4(comb_1_ss4));
  Priority_Encoder priority_encoder_1 (
    .in0(comb_1_ss0), .in1(comb_1_ss1), .in2(comb_1_ss2), .in3(comb_1_ss3), .in4(comb_1_ss4), .in5(1'b0),
    .in6(1'b0), .in7(1'b0), .out(next));  // open: en_in, gs, en_out
endmodule

module comb (
  input  S0,
  input  S1,
  input  S2,
  input  S3,
  input  S4,
  input  I1,
  input  I2,
  output SS0,
  output SS1,
  output SS2,
  output SS3,
  output SS4
);

  wire and_1_out, and_2_out, not_1_out, not_2_out, not_3_out, not_4_out, not_5_out, or_1_out, or_2_out,
       or_3_out, or_4_out;

  or or_1 (or_1_out, S0, S4);
  not not_1 (not_1_out, I2);
  or or_2 (or_2_out, S0, S3, S4);
  not not_2 (not_2_out, I1);
  or or_3 (or_3_out, S1, S2);
  not not_3 (not_3_out, I1);
  or or_4 (or_4_out, S1, S2);
  not not_4 (not_4_out, I2);
  not not_5 (not_5_out, I2);
  and and_1 (and_1_out, I1, I2);
  and and_2 (and_2_out, or_1_out, not_1_out);
  and and_3 (SS1, or_2_out, not_2_out, I2);
  and and_4 (SS2, or_3_out, not_3_out, I2);
  and and_5 (SS3, or_4_out, not_4_out);
  and and_6 (SS4, S3, not_5_out);
  or or_5 (SS0, and_1_out, and_2_out);
endmodule

module \reg  (
  input  [2:0] D,
  input  CLK,
  input  CLR,
  output [2:0] Q
);

  wire [2:0] multiplexer_1_out;

  Multiplexer #(.width(3)) multiplexer_1 (.in0(D), .in1(3'b000), .out(multiplexer_1_out), .sel(CLR));  // open: en
  Register #(.width(3)) register_1 (.D(multiplexer_1_out), .Q(Q), .clk(CLK));  // open: en, clr
endmodule

module out (
  input  [1:0] In,
  input  [2:0] state,
  output Z
);

  wire [2:0] trans_1_next;

  trans trans_1 (.state(state), .In(In), .next(trans_1_next));
  Comparator #(.width(3)) comparator_1 (.a(trans_1_next), .b(3'b100), .eq(Z));  // open: gt, lt
endmodule

module test (
  output out_1,
  output out_2
);

  wire clock_1_out;
  wire [2:0] rom_1_data;
  wire [7:0] counter_1_q;

  Clock clock_1 (.out(clock_1_out));
  Counter counter_1 (.Q(counter_1_q), .carry(out_2), .clk(clock_1_out));  // open: load, D, count, clr
  ROM #(.dataWidth(3)) rom_1 (.addr(counter_1_q), .data(rom_1_data));  // open: sel
  fsm fsm_1 (.CLR(rom_1_data[0]), .In(rom_1_data[2:1]), .Z(out_1));
endmodule
