// Logisim project cpu - 副本.circ as structural Verilog
module IFU (
  input  Clk,
  input  Reset,
  input  nPC_ct,
  input  [15:0] Imm,
  output [31:0] Instr
);

  wire [31:0] adder_1_out, adder_2_out, multiplexer_1_out, register_1_q, signed_ext_1_out_2;

  signed_ext signed_ext_1 (.in_1(Imm), .out_2(signed_ext_1_out_2));
  Adder #(.width(32)) adder_1 (.a(register_1_q), .b(32'h4), .out(adder_1_out));  // open: cin, cout
  Multiplexer #(.width(32)) multiplexer_1 (
    .in0(adder_1_out), .in1(adder_2_out), .out(multiplexer_1_out), .sel(nPC_ct));  // open: en
  Adder #(.width(32)) adder_2 (.a(adder_1_out), .b(signed_ext_1_out_2), .out(adder_2_out));  // open: cin, cout
  Register #(.width(32)) register_1 (.D(multiplexer_1_out), .Q(register_1_q), .clk(Clk), .clr(Reset));  // open: en
  ROM #(.addrWidth(5), .dataWidth(32)) rom_1 (.addr(register_1_q[4:0]), .data(Instr));  // open: sel

  // Other names for the same wires on the sheet: control = nPC_ct
endmodule

module signed_ext (
  input  [15:0] in_1,
  output [31:0] out_2
);


  assign out_2 = {{17{in_1[15]}}, in_1[14:0]};
endmodule
