// Logisim project cpu.circ as structural Verilog: 22 circuits, main circuit main
module main (
  input  Reset,
  output [31:0] out_2,
  output out_3,
  output [4:0] out_4,
  output [31:0] out_5,
  output out_6,
  output [4:0] out_7,
  output [31:0] out_8
);

  wire alu_1_zero, ALUSrc, Br, Clk, DatatoReg, IFUIMM, Reg3Src;
  wire [1:0] bc_1_npc_ct, EXTCtrl;
  wire [2:0] ALUCtrl;
  wire [31:0] dm_1_rd, ext_1_result, grf_1_rd1, MemAddr, multiplexer_1_out, multiplexer_3_out, PC,
       signed_ext_1_out_2;

  Multiplexer #(.width(32)) multiplexer_1 (
    .in0({PC[31:28], out_2[25:0], 2'b00}), .in1(signed_ext_1_out_2), .out(multiplexer_1_out), .sel(IFUIMM));  // open: en
  Clock u_Clk (.out(Clk));
  IFU ifu_1 (.Clk(Clk), .Reset(Reset), .nPC_ct(bc_1_npc_ct), .Imm(multiplexer_1_out), .Instr(out_2), .PC(PC));
  signed_ext signed_ext_1 (.in_1(out_2[15:0]), .out_2(signed_ext_1_out_2));
  Multiplexer #(.width(5)) multiplexer_2 (
    .in0(out_2[15:11]), .in1(out_2[20:16]), .out(out_4), .sel(Reg3Src));  // open: en
  Control control_1 (
    .funct(out_2[5:0]), .opcode(out_2[31:26]), .Br(Br), .Reg3Src(Reg3Src), .DatatoReg(DatatoReg),
    .RegWE(out_3), .ALUSrc(ALUSrc), .ALUCtrl(ALUCtrl), .DMWE(out_6), .EXTCtrl(EXTCtrl), .J(bc_1_npc_ct[1]),
    .IFUIMM(IFUIMM));
  GRF grf_1 (
    .A1(out_2[25:21]), .A2(out_2[20:16]), .A3(out_4), .WD(out_5), .RD1(grf_1_rd1), .RD2(out_8), .Clk(Clk),
    .Reset(Reset), .WE(out_3));
  EXT ext_1 (.Imm(out_2[15:0]), .Result(ext_1_result), .ExtCtrl(EXTCtrl));
  Multiplexer #(.width(32)) multiplexer_3 (
    .in0(out_8), .in1(ext_1_result), .out(multiplexer_3_out), .sel(ALUSrc));  // open: en
  BC bc_1 (.Br(Br), .Zero(alu_1_zero), .nPC_ct(bc_1_npc_ct[0]));
  ALU alu_1 (
    .SrcA(grf_1_rd1), .SrcB(multiplexer_3_out), .Zero(alu_1_zero),
    .ALUResult({MemAddr[31:7], out_7, MemAddr[1:0]}), .ALUCtrl(ALUCtrl), .Shamt(out_2[10:6]));
  Multiplexer #(.width(32)) multiplexer_4 (
    .in0({MemAddr[31:7], out_7, MemAddr[1:0]}), .in1(dm_1_rd), .out(out_5), .sel(DatatoReg));  // open: en
  DM dm_1 (.A({MemAddr[31:7], out_7, MemAddr[1:0]}), .WD(out_8), .RD(dm_1_rd), .Clk(Clk), .Reset(Reset), .WE(out_6));

  // Other names for the same wires on the sheet: DMWE = out_6; Instr[31:0] = out_2; MemAddr[6:2] = out_7;
  //   MemData[31:0] = out_8; RegAddr[4:0] = out_4; RegData[31:0] = out_5; RegWE = out_3
endmodule

module IFU (
  input  Clk,
  input  Reset,
  input  [1:0] nPC_ct,
  input  [31:0] Imm,
  output [31:0] Instr,
  output [31:0] PC
);

  wire [31:0] adder_2_out, cur_PC, multiplexer_1_out, shifter_1_out;

  Adder #(.width(32)) adder_1 (.a(cur_PC), .b(32'h4), .out(PC));  // open: cin, cout
  Shifter #(.width(32)) shifter_1 (.in(Imm), .\dist (5'b00010), .out(shifter_1_out));
  Adder #(.width(32)) adder_2 (.a(PC), .b(shifter_1_out), .out(adder_2_out));  // open: cin, cout
  Multiplexer #(.select(2), .width(32)) multiplexer_1 (
    .in0(PC), .in1(adder_2_out), .in2(Imm), .in3(Imm), .out(multiplexer_1_out), .sel(nPC_ct));  // open: en
  Register #(.width(32)) register_1 (.D(multiplexer_1_out), .Q(cur_PC), .clk(Clk), .clr(Reset));  // open: en
  ROM #(.addrWidth(5), .dataWidth(32)) rom_1 (.addr(cur_PC[6:2]), .data(Instr));  // open: sel

  // Other names for the same wires on the sheet: control[1:0] = nPC_ct; PC_4[31:0] = PC

  // Notes on the sheet:
  //   contents of rom_1 (hex, n*v repeats v):
  //   34120000 34087111 3c080007 35088000 ae480000 34100001 34110020 1211000b 0 34080004 2489021 8e48fffc
  //   34098000 1094023 ae480000 34080001 2088021 8000c07
endmodule

module GRF (
  input  Clk,
  input  Reset,
  input  WE,
  input  [4:0] A1,
  input  [4:0] A2,
  input  [4:0] A3,
  input  [31:0] WD,
  output [31:0] RD1,
  output [31:0] RD2
);

  wire comparator_1_eq;
  wire [31:0] multiplexer_1_out;

  Comparator #(.width(5), .mode("unsigned")) comparator_1 (
    .a(A3), .b({5{1'b0}}), .eq(comparator_1_eq));  // open: gt, lt
  Multiplexer #(.width(32)) multiplexer_1 (
    .in0(WD), .in1({32{1'b0}}), .out(multiplexer_1_out), .sel(comparator_1_eq));  // open: en
  _32_reg u_32_reg_1 (
    .A1(A1), .A2(A2), .A3(A3), .WD(multiplexer_1_out), .clk(Clk), .reset(Reset), .WE(WE), .RD1(RD1), .RD2(RD2));
endmodule

module ALU (
  input  [31:0] SrcA,
  input  [31:0] SrcB,
  input  [4:0] Shamt,
  input  [2:0] ALUCtrl,
  output Zero,
  output [31:0] ALUResult
);

  wire [31:0] R1, R2, R3, R4, R5;

  Subtractor #(.width(32)) subtractor_1 (.a(SrcA), .b(SrcB), .out(R4));  // open: bin, bout
  Adder #(.width(32)) adder_1 (.a(SrcA), .b(SrcB), .out(R1));  // open: cin, cout
  Subtractor #(.width(32)) subtractor_2 (.a(SrcA), .b(SrcB), .out(R2));  // open: bin, bout
  Shifter #(.width(32)) shifter_1 (.in(SrcB), .\dist (Shamt), .out(R5));
  Multiplexer #(.select(3), .width(32)) multiplexer_1 (
    .in0(R1), .in1(R2), .in2(R3), .in3(R4), .in4(R5), .out(ALUResult), .sel(ALUCtrl));  // open: in5, in6, in7, en
  Comparator #(.width(32)) comparator_1 (.a({32{1'b0}}), .b(ALUResult), .eq(Zero));  // open: gt, lt
  assign R3 = SrcA | SrcB;  // OR_Gate or_1, 32 bits wide

  // Other names for the same wires on the sheet: A[31:0] = SrcA; B[31:0] = SrcB; CT[2:0] = ALUCtrl
endmodule

module DM (
  input  [31:0] A,
  input  [31:0] WD,
  input  Clk,
  input  Reset,
  input  WE,
  output [31:0] RD
);

  RAM #(.addrWidth(5), .dataWidth(32), .bus("separate")) ram_1 (
    .addr(A[6:2]), .din(WD), .data(RD), .str(WE), .clk(Clk), .clr(Reset));  // open: sel, ld
endmodule

module EXT (
  input  [15:0] Imm,
  input  [1:0] ExtCtrl,
  output [31:0] Result
);

  wire [31:0] bit_extender_1_out, bit_extender_2_out, bit_extender_3_out;

  assign bit_extender_1_out = {{16{1'b0}}, Imm};  // Bit_Extender bit_extender_1
  assign bit_extender_2_out = {{16{Imm[15]}}, Imm};  // Bit_Extender bit_extender_2
  assign bit_extender_3_out = {{16{1'b1}}, Imm};  // Bit_Extender bit_extender_3
  Multiplexer #(.select(2), .width(32)) multiplexer_1 (
    .in0(bit_extender_1_out), .in1(bit_extender_2_out), .in2({Imm, {16{1'b0}}}), .in3(bit_extender_3_out),
    .out(Result), .sel(ExtCtrl));  // open: en
endmodule

module Control (
  input  [5:0] funct,
  input  [5:0] opcode,
  output J,
  output Br,
  output Reg3Src,
  output DatatoReg,
  output RegWE,
  output ALUSrc,
  output [2:0] ALUCtrl,
  output DMWE,
  output [1:0] EXTCtrl,
  output IFUIMM
);

  wire addu, beq, j_t, lui, lw, op_decode_1_r, ori, sll, subu, sw;

  op_decode op_decode_1 (
    .op_5(opcode[5]), .op_4(opcode[4]), .op_3(opcode[3]), .op_2(opcode[2]), .op_1(opcode[1]),
    .op_0(opcode[0]), .R(op_decode_1_r), .ori(ori), .lw(lw), .sw(sw), .beq(beq), .lui(lui), .j(j_t));
  buf or_1 (Br, beq);  // OR_Gate
  funct_decode funct_decode_1 (
    .is_R(op_decode_1_r), .funct_5(funct[5]), .funct_4(funct[4]), .funct_3(funct[3]), .funct_2(funct[2]),
    .funct_1(funct[1]), .funct_0(funct[0]), .addu(addu), .subu(subu), .sll(sll));
  or or_2 (Reg3Src, ori, lw, lui, sll);
  buf or_3 (DatatoReg, lw);  // OR_Gate
  or or_4 (RegWE, addu, subu, ori, lw, lui, sll);
  or or_5 (ALUSrc, ori, lw, sw, lui);
  buf _2 (ALUCtrl[2], sll);  // OR_Gate
  or _0 (ALUCtrl[0], subu, beq);
  or _1 (ALUCtrl[1], ori, beq);
  buf or_6 (DMWE, sw);  // OR_Gate
  buf _1_2 (EXTCtrl[1], lui);  // OR_Gate
  or _0_2 (EXTCtrl[0], lw, sw);
  buf or_7 (J, j_t);  // OR_Gate
  buf or_8 (IFUIMM, beq);  // OR_Gate

  // Other names for the same wires on the sheet: Jump = J
endmodule

module BC (
  input  Br,
  input  Zero,
  output nPC_ct
);

  and and_1 (nPC_ct, Br, Zero);
endmodule

module op_decode (
  input  op_5,
  input  op_4,
  input  op_3,
  input  op_2,
  input  op_1,
  input  op_0,
  output R,
  output ori,
  output lw,
  output sw,
  output beq,
  output lui,
  output j
);

  wire not_1_out, not_2_out, not_3_out, not_4_out, not_5_out, not_6_out;

  not not_1 (not_1_out, op_5);
  not not_2 (not_2_out, op_4);
  not not_3 (not_3_out, op_3);
  not not_4 (not_4_out, op_2);
  not not_5 (not_5_out, op_1);
  not not_6 (not_6_out, op_0);
  and and_1 (R, not_1_out, not_2_out, not_3_out, not_4_out, not_5_out, not_6_out);
  and and_2 (ori, not_1_out, not_2_out, op_3, op_2, not_5_out, op_0);
  and and_3 (lw, op_5, not_2_out, not_3_out, not_4_out, op_1, op_0);
  and and_4 (sw, op_5, not_2_out, op_3, not_4_out, op_1, op_0);
  and and_5 (beq, not_1_out, not_2_out, not_3_out, op_2, not_5_out, not_6_out);
  and and_6 (lui, not_1_out, not_2_out, op_3, op_2, op_1, op_0);
  and and_7 (j, not_1_out, not_2_out, not_3_out, not_4_out, op_1, not_6_out);
endmodule

module funct_decode (
  input  funct_5,
  input  funct_4,
  input  funct_3,
  input  funct_2,
  input  funct_1,
  input  funct_0,
  input  is_R,
  output addu,
  output subu,
  output sll
);

  wire and_1_out, and_2_out, and_3_out, not_1_out, not_2_out, not_3_out, not_4_out, not_5_out, not_6_out;

  not not_1 (not_1_out, funct_5);
  not not_2 (not_2_out, funct_4);
  not not_3 (not_3_out, funct_3);
  not not_4 (not_4_out, funct_2);
  not not_5 (not_5_out, funct_0);
  not not_6 (not_6_out, funct_1);
  and and_1 (and_1_out, funct_5, not_2_out, not_3_out, not_4_out, not_6_out, funct_0);
  and and_2 (and_2_out, funct_5, not_2_out, not_3_out, not_4_out, funct_1, funct_0);
  and and_3 (and_3_out, not_1_out, not_2_out, not_3_out, not_4_out, not_6_out, not_5_out);
  and and_4 (addu, and_1_out, is_R);
  and and_5 (subu, and_2_out, is_R);
  and and_6 (sll, and_3_out, is_R);
endmodule

module signed_ext (
  input  [15:0] in_1,
  output [31:0] out_2
);


  assign out_2 = {{17{in_1[15]}}, in_1[14:0]};
endmodule

module zero_ext (
  input  [15:0] in_1,
  output [31:0] out_2
);


  assign out_2 = {{16{1'b0}}, in_1};
endmodule

module single_reg (
  input  [31:0] in_1,
  input  clk,
  input  en,
  input  reset,
  output [31:0] out_5
);

  wire [31:0] multiplexer_1_out, multiplexer_2_out;

  Multiplexer #(.width(32)) multiplexer_1 (.in0(out_5), .in1(in_1), .out(multiplexer_1_out), .sel(en));  // open: en
  Multiplexer #(.width(32)) multiplexer_2 (
    .in0(multiplexer_1_out), .in1({32{1'b0}}), .out(multiplexer_2_out), .sel(reset));  // open: en
  Register #(.width(32)) register_1 (.D(multiplexer_2_out), .en(1'b1), .Q(out_5), .clk(clk), .clr(reset));
endmodule

module _2_reg (
  input  A1,
  input  clk,
  input  reset,
  input  WE,
  input  A2,
  input  A3,
  input  [31:0] WD,
  output [31:0] RD1,
  output [31:0] RD2
);

  wire not_1_out, WE0, WE1;
  wire [31:0] single_reg_1_out_5, single_reg_2_out_5;

  not not_1 (not_1_out, A3);
  and and_1 (WE0, WE, not_1_out);
  and and_2 (WE1, WE, A3);
  single_reg single_reg_1 (.in_1(WD), .out_5(single_reg_1_out_5), .clk(clk), .en(WE0), .reset(reset));
  single_reg single_reg_2 (.in_1(WD), .out_5(single_reg_2_out_5), .clk(clk), .en(WE1), .reset(reset));
  Multiplexer #(.width(32)) multiplexer_1 (
    .in0(single_reg_1_out_5), .in1(single_reg_2_out_5), .out(RD1), .sel(A1));  // open: en
  Multiplexer #(.width(32)) multiplexer_2 (
    .in0(single_reg_1_out_5), .in1(single_reg_2_out_5), .out(RD2), .sel(A2));  // open: en
endmodule

module _4_reg (
  input  clk,
  input  reset,
  input  WE,
  input  [1:0] A1,
  input  [1:0] A2,
  input  [1:0] A3,
  input  [31:0] WD,
  output [31:0] RD1,
  output [31:0] RD2
);

  wire not_1_out, WE0, WE1;
  wire [31:0] n2_reg_1_rd1, n2_reg_1_rd2, n2_reg_2_rd1, n2_reg_2_rd2;

  not not_1 (not_1_out, A3[1]);
  and and_1 (WE0, WE, not_1_out);
  and and_2 (WE1, WE, A3[1]);
  _2_reg u_2_reg_1 (
    .A1(A1[0]), .A2(A2[0]), .A3(A3[0]), .WD(WD), .clk(clk), .reset(reset), .WE(WE0), .RD1(n2_reg_1_rd1),
    .RD2(n2_reg_1_rd2));
  _2_reg u_2_reg_2 (
    .A1(A1[0]), .A2(A2[0]), .A3(A3[0]), .WD(WD), .clk(clk), .reset(reset), .WE(WE1), .RD1(n2_reg_2_rd1),
    .RD2(n2_reg_2_rd2));
  Multiplexer #(.width(32)) multiplexer_1 (.in0(n2_reg_1_rd1), .in1(n2_reg_2_rd1), .out(RD1), .sel(A1[1]));  // open: en
  Multiplexer #(.width(32)) multiplexer_2 (.in0(n2_reg_1_rd2), .in1(n2_reg_2_rd2), .out(RD2), .sel(A2[1]));  // open: en

  // Other names for the same wires on the sheet: A1_next = A1[0]; A1_now = A1[1]; A2_next = A2[0]; A2_now = A2[1];
  //   A3_next = A3[0]; A3_now = A3[1]
endmodule

module _8_reg (
  input  clk,
  input  reset,
  input  WE,
  input  [2:0] A1,
  input  [2:0] A2,
  input  [2:0] A3,
  input  [31:0] WD,
  output [31:0] RD1,
  output [31:0] RD2
);

  wire not_1_out, WE0, WE1;
  wire [31:0] n4_reg_1_rd1, n4_reg_1_rd2, n4_reg_2_rd1, n4_reg_2_rd2;

  not not_1 (not_1_out, A3[2]);
  and and_1 (WE0, WE, not_1_out);
  and and_2 (WE1, WE, A3[2]);
  _4_reg u_4_reg_1 (
    .A1(A1[1:0]), .A2(A2[1:0]), .A3(A3[1:0]), .WD(WD), .clk(clk), .reset(reset), .WE(WE0),
    .RD1(n4_reg_1_rd1), .RD2(n4_reg_1_rd2));
  _4_reg u_4_reg_2 (
    .A1(A1[1:0]), .A2(A2[1:0]), .A3(A3[1:0]), .WD(WD), .clk(clk), .reset(reset), .WE(WE1),
    .RD1(n4_reg_2_rd1), .RD2(n4_reg_2_rd2));
  Multiplexer #(.width(32)) multiplexer_1 (.in0(n4_reg_1_rd1), .in1(n4_reg_2_rd1), .out(RD1), .sel(A1[2]));  // open: en
  Multiplexer #(.width(32)) multiplexer_2 (.in0(n4_reg_1_rd2), .in1(n4_reg_2_rd2), .out(RD2), .sel(A2[2]));  // open: en

  // Other names for the same wires on the sheet: A1_next[1:0] = A1[1:0]; A1_now = A1[2]; A2_next[1:0] = A2[1:0];
  //   A2_now = A2[2]; A3_next[1:0] = A3[1:0]; A3_now = A3[2]
endmodule

module _16_reg (
  input  clk,
  input  reset,
  input  WE,
  input  [3:0] A1,
  input  [3:0] A2,
  input  [3:0] A3,
  input  [31:0] WD,
  output [31:0] RD1,
  output [31:0] RD2
);

  wire not_1_out, WE0, WE1;
  wire [31:0] n8_reg_1_rd1, n8_reg_1_rd2, n8_reg_2_rd1, n8_reg_2_rd2;

  not not_1 (not_1_out, A3[3]);
  and and_1 (WE0, WE, not_1_out);
  and and_2 (WE1, WE, A3[3]);
  _8_reg u_8_reg_1 (
    .A1(A1[2:0]), .A2(A2[2:0]), .A3(A3[2:0]), .WD(WD), .clk(clk), .reset(reset), .WE(WE0),
    .RD1(n8_reg_1_rd1), .RD2(n8_reg_1_rd2));
  _8_reg u_8_reg_2 (
    .A1(A1[2:0]), .A2(A2[2:0]), .A3(A3[2:0]), .WD(WD), .clk(clk), .reset(reset), .WE(WE1),
    .RD1(n8_reg_2_rd1), .RD2(n8_reg_2_rd2));
  Multiplexer #(.width(32)) multiplexer_1 (.in0(n8_reg_1_rd1), .in1(n8_reg_2_rd1), .out(RD1), .sel(A1[3]));  // open: en
  Multiplexer #(.width(32)) multiplexer_2 (.in0(n8_reg_1_rd2), .in1(n8_reg_2_rd2), .out(RD2), .sel(A2[3]));  // open: en

  // Other names for the same wires on the sheet: A1_next[2:0] = A1[2:0]; A1_now = A1[3]; A2_next[2:0] = A2[2:0];
  //   A2_now = A2[3]; A3_next[2:0] = A3[2:0]; A3_now = A3[3]
endmodule

module _32_reg (
  input  clk,
  input  reset,
  input  WE,
  input  [4:0] A1,
  input  [4:0] A2,
  input  [4:0] A3,
  input  [31:0] WD,
  output [31:0] RD1,
  output [31:0] RD2
);

  wire not_1_out, WE0, WE1;
  wire [31:0] n16_reg_1_rd1, n16_reg_1_rd2, n16_reg_2_rd1, n16_reg_2_rd2;

  not not_1 (not_1_out, A3[4]);
  and and_1 (WE0, WE, not_1_out);
  and and_2 (WE1, WE, A3[4]);
  _16_reg u_16_reg_1 (
    .A1(A1[3:0]), .A2(A2[3:0]), .A3(A3[3:0]), .WD(WD), .clk(clk), .reset(reset), .WE(WE0),
    .RD1(n16_reg_1_rd1), .RD2(n16_reg_1_rd2));
  _16_reg u_16_reg_2 (
    .A1(A1[3:0]), .A2(A2[3:0]), .A3(A3[3:0]), .WD(WD), .clk(clk), .reset(reset), .WE(WE1),
    .RD1(n16_reg_2_rd1), .RD2(n16_reg_2_rd2));
  Multiplexer #(.width(32)) multiplexer_1 (
    .in0(n16_reg_1_rd1), .in1(n16_reg_2_rd1), .out(RD1), .sel(A1[4]));  // open: en
  Multiplexer #(.width(32)) multiplexer_2 (
    .in0(n16_reg_1_rd2), .in1(n16_reg_2_rd2), .out(RD2), .sel(A2[4]));  // open: en

  // Other names for the same wires on the sheet: A1_next[3:0] = A1[3:0]; A1_now = A1[4]; A2_next[3:0] = A2[3:0];
  //   A2_now = A2[4]; A3_next[3:0] = A3[3:0]; A3_now = A3[4]
endmodule

module spliter_nothing (
);
endmodule

module test (
  input  in_1
);

  wire cpu_out_3, cpu_out_6;
  wire [4:0] cpu_out_4, cpu_out_7;
  wire [31:0] cpu_out_2, cpu_out_5, cpu_out_8;

  main cpu (
    .Reset(in_1), .out_2(cpu_out_2), .out_3(cpu_out_3), .out_4(cpu_out_4), .out_5(cpu_out_5),
    .out_6(cpu_out_6), .out_7(cpu_out_7), .out_8(cpu_out_8));
  // Probe on cpu_out_2
  // Probe on cpu_out_3
  // Probe on cpu_out_4
  // Probe on cpu_out_5
  // Probe on cpu_out_6
  // Probe on cpu_out_7
  // Probe on cpu_out_8
endmodule

module jcalc (
  input  [25:0] imm,
  input  [31:0] pc,
  output [31:0] npc
);


  assign npc = {pc[31:28], imm, 2'b00};
endmodule

module try_sb (
  input  [31:0] in_1,
  input  in_2,
  input  [31:0] in_3
);

  wire clock_1_out;
  wire [31:0] and_1_out, D, NextD, not_1_out, shifter_1_out, shifter_2_out;

  assign not_1_out = ~shifter_1_out;  // NOT_Gate not_1, 32 bits wide
  Shifter #(.width(32)) shifter_1 (.in(32'hff), .\dist ({in_1[1:0], 3'b000}), .out(shifter_1_out));
  Shifter #(.width(32)) shifter_2 (.in(in_3), .\dist ({in_1[1:0], 3'b000}), .out(shifter_2_out));
  Clock clock_1 (.out(clock_1_out));
  DM dm_1 (.A(in_1), .WD(NextD), .RD(D), .Clk(clock_1_out), .WE(in_2));  // open: Reset
  assign and_1_out = not_1_out & D;  // AND_Gate and_1, 32 bits wide
  assign NextD = and_1_out | shifter_2_out;  // OR_Gate or_1, 32 bits wide

  // Other names for the same wires on the sheet: A[31:0] = in_1
endmodule
