// Logisim project CPU-lzb.circ as structural Verilog: 11 circuits, main circuit main
module main (
  input  in_1,
  output [31:0] out_2,
  output out_3,
  output [4:0] out_4,
  output [31:0] out_5,
  output out_6,
  output [4:0] out_7,
  output [31:0] out_8
);

  CPU cpu_1 (
    .Reset(in_1), .out_2(out_2), .out_3(out_3), .out_4(out_4), .out_5(out_5), .out_6(out_6), .out_7(out_7),
    .out_8(out_8));
endmodule

module GRF (
  input  clk,
  input  reset,
  input  WE,
  input  [4:0] A1,
  input  [4:0] A2,
  input  [4:0] A3,
  input  [31:0] WD,
  output [31:0] out_8,
  output [31:0] out_9
);

  wire W1, W2, W3, W4, W5, W6, W7, W8, W9, W10, W11, W12, W13, W14, W15, W16, W17, W18, W19, W20, W21, W22,
       W23, W24, W25, W26, W27, W28, W29, W30, W31;
  wire [31:0] _0, _1, _2, _3, _4, _5, _6, _7, _8, _9, _10, _11, _12, _13, _14, _15, _16, _17, _18, _19, _20,
       _21, _22, _23, _24, _25, _26, _27, _28, _29, _30, _31;

  Register #(.width(32)) register_1 (.D(WD), .en(1'b0), .Q(_0), .clk(clk), .clr(reset));
  Register #(.width(32)) register_2 (.D(WD), .en(W1), .Q(_1), .clk(clk), .clr(reset));
  Register #(.width(32)) register_3 (.D(WD), .en(W2), .Q(_2), .clk(clk), .clr(reset));
  Register #(.width(32)) register_4 (.D(WD), .en(W3), .Q(_3), .clk(clk), .clr(reset));
  Register #(.width(32)) register_5 (.D(WD), .en(W4), .Q(_4), .clk(clk), .clr(reset));
  Demultiplexer #(.select(5)) demultiplexer_1 (
    .out1(W1), .out2(W2), .out3(W3), .out4(W4), .out5(W5), .out6(W6), .out7(W7), .out8(W8), .out9(W9),
    .out10(W10), .out11(W11), .out12(W12), .out13(W13), .out14(W14), .out15(W15), .out16(W16), .out17(W17),
    .out18(W18), .out19(W19), .out20(W20), .out21(W21), .out22(W22), .out23(W23), .out24(W24), .out25(W25),
    .out26(W26), .out27(W27), .out28(W28), .out29(W29), .out30(W30), .out31(W31), .in(WE), .sel(A3));  // open: out0, en
  Register #(.width(32)) register_6 (.D(WD), .en(W5), .Q(_5), .clk(clk), .clr(reset));
  Register #(.width(32)) register_7 (.D(WD), .en(W6), .Q(_6), .clk(clk), .clr(reset));
  Register #(.width(32)) register_8 (.D(WD), .en(W7), .Q(_7), .clk(clk), .clr(reset));
  Register #(.width(32)) register_9 (.D(WD), .en(W8), .Q(_8), .clk(clk), .clr(reset));
  Register #(.width(32)) register_10 (.D(WD), .en(W9), .Q(_9), .clk(clk), .clr(reset));
  Register #(.width(32)) register_11 (.D(WD), .en(W10), .Q(_10), .clk(clk), .clr(reset));
  Register #(.width(32)) register_12 (.D(WD), .en(W11), .Q(_11), .clk(clk), .clr(reset));
  Register #(.width(32)) register_13 (.D(WD), .en(W12), .Q(_12), .clk(clk), .clr(reset));
  Register #(.width(32)) register_14 (.D(WD), .en(W13), .Q(_13), .clk(clk), .clr(reset));
  Register #(.width(32)) register_15 (.D(WD), .en(W14), .Q(_14), .clk(clk), .clr(reset));
  Register #(.width(32)) register_16 (.D(WD), .en(W15), .Q(_15), .clk(clk), .clr(reset));
  Register #(.width(32)) register_17 (.D(WD), .en(W16), .Q(_16), .clk(clk), .clr(reset));
  Register #(.width(32)) register_18 (.D(WD), .en(W17), .Q(_17), .clk(clk), .clr(reset));
  Register #(.width(32)) register_19 (.D(WD), .en(W18), .Q(_18), .clk(clk), .clr(reset));
  Register #(.width(32)) register_20 (.D(WD), .en(W19), .Q(_19), .clk(clk), .clr(reset));
  Register #(.width(32)) register_21 (.D(WD), .en(W20), .Q(_20), .clk(clk), .clr(reset));
  Register #(.width(32)) register_22 (.D(WD), .en(W21), .Q(_21), .clk(clk), .clr(reset));
  Register #(.width(32)) register_23 (.D(WD), .en(W22), .Q(_22), .clk(clk), .clr(reset));
  Register #(.width(32)) register_24 (.D(WD), .en(W23), .Q(_23), .clk(clk), .clr(reset));
  Register #(.width(32)) register_25 (.D(WD), .en(W24), .Q(_24), .clk(clk), .clr(reset));
  Register #(.width(32)) register_26 (.D(WD), .en(W25), .Q(_25), .clk(clk), .clr(reset));
  Register #(.width(32)) register_27 (.D(WD), .en(W26), .Q(_26), .clk(clk), .clr(reset));
  Register #(.width(32)) register_28 (.D(WD), .en(W27), .Q(_27), .clk(clk), .clr(reset));
  Register #(.width(32)) register_29 (.D(WD), .en(W28), .Q(_28), .clk(clk), .clr(reset));
  Register #(.width(32)) register_30 (.D(WD), .en(W29), .Q(_29), .clk(clk), .clr(reset));
  Register #(.width(32)) register_31 (.D(WD), .en(W30), .Q(_30), .clk(clk), .clr(reset));
  Register #(.width(32)) register_32 (.D(WD), .en(W31), .Q(_31), .clk(clk), .clr(reset));
  Multiplexer #(.select(5), .width(32)) multiplexer_1 (
    .in0(_0), .in1(_1), .in2(_2), .in3(_3), .in4(_4), .in5(_5), .in6(_6), .in7(_7), .in8(_8), .in9(_9),
    .in10(_10), .in11(_11), .in12(_12), .in13(_13), .in14(_14), .in15(_15), .in16(_16), .in17(_17),
    .in18(_18), .in19(_19), .in20(_20), .in21(_21), .in22(_22), .in23(_23), .in24(_24), .in25(_25),
    .in26(_26), .in27(_27), .in28(_28), .in29(_29), .in30(_30), .in31(_31), .out(out_8), .sel(A1));  // open: en
  Multiplexer #(.select(5), .width(32)) multiplexer_2 (
    .in0(_0), .in1(_1), .in2(_2), .in3(_3), .in4(_4), .in5(_5), .in6(_6), .in7(_7), .in8(_8), .in9(_9),
    .in10(_10), .in11(_11), .in12(_12), .in13(_13), .in14(_14), .in15(_15), .in16(_16), .in17(_17),
    .in18(_18), .in19(_19), .in20(_20), .in21(_21), .in22(_22), .in23(_23), .in24(_24), .in25(_25),
    .in26(_26), .in27(_27), .in28(_28), .in29(_29), .in30(_30), .in31(_31), .out(out_9), .sel(A2));  // open: en

  // Other names for the same wires on the sheet: Data[31:0] = WD
endmodule

module ALU (
  input  [3:0] ALUCtrl,
  input  [31:0] SrcA,
  input  [31:0] SrcB,
  output Zero,
  output [31:0] ALURes
);

  wire [0:0] R8;
  wire [31:0] R0, R1, R2, R3, R4, R5, R6;

  Adder #(.width(32)) adder_1 (.a(SrcA), .b(SrcB), .out(R0));  // open: cin, cout
  Subtractor #(.width(32)) subtractor_1 (.a(SrcA), .b(SrcB), .out(R1));  // open: bin, bout
  assign R2 = SrcA & SrcB;  // AND_Gate and_1, 32 bits wide
  assign R3 = SrcA | SrcB;  // OR_Gate or_1, 32 bits wide
  Shifter #(.width(32)) shifter_1 (.in(SrcA), .\dist (SrcB[4:0]), .out(R4));
  Shifter #(.width(32), .shift("lr")) shifter_2 (.in(SrcA), .\dist (SrcB[4:0]), .out(R5));
  Multiplexer #(.select(4), .width(32)) multiplexer_1 (
    .in0(R0), .in1(R1), .in2(R2), .in3(R3), .in4(R4), .in5(R5), .in6(R6), .in7({SrcB[15:0], {16{1'b0}}}),
    .in8({{31{1'b0}}, R8[0]}), .out(ALURes), .sel(ALUCtrl));  // open: in9, in10, in11, in12, in13, in14, in15, en
  Shifter #(.width(32), .shift("ar")) shifter_3 (.in(SrcA), .\dist (SrcB[4:0]), .out(R6));
  // Probe on ALURes
  Comparator #(.width(32), .mode("unsigned")) comparator_1 (.a({32{1'b0}}), .b(ALURes), .eq(Zero));  // open: gt, lt
  Comparator #(.width(32), .mode("unsigned")) comparator_2 (.a(SrcA), .b(SrcB), .lt(R8[0]));  // open: gt, eq

  // Other names for the same wires on the sheet: R7[31:16] = SrcB[15:0]
endmodule

module EXT (
  input  [15:0] Imm,
  input  ExtOp,
  output [31:0] ExtRes
);

  wire [31:16] \signed ;

  Multiplexer #(.width(16)) multiplexer_1 (
    .in0({16{1'b0}}), .in1({16{1'b1}}), .out(\signed ), .sel(Imm[15]));  // open: en
  Multiplexer #(.width(32)) multiplexer_2 (
    .in0({{16{1'b0}}, Imm}), .in1({\signed , Imm}), .out(ExtRes), .sel(ExtOp));  // open: en

  // Other names for the same wires on the sheet: signed[15:0] = Imm; zero[15:0] = Imm
endmodule

module DM (
  input  Clk,
  input  WE,
  input  Reset,
  input  [31:0] Addr,
  input  [31:0] Data,
  output [31:0] RD,
  output [4:0] out_7
);

  RAM #(.addrWidth(5), .dataWidth(32), .bus("separate")) ram_1 (
    .addr(Addr[6:2]), .din(Data), .data(RD), .str(WE), .clk(Clk), .clr(Reset));  // open: sel, ld

  assign out_7 = Addr[6:2];

  // Other names for the same wires on the sheet: Addr_t[4:0] = Addr[6:2]; Addr_tb[4:0] = Addr[6:2]
endmodule

module IFU (
  input  PCSrc,
  input  Clk,
  input  Reset,
  input  [15:0] Imm,
  output [31:0] Inst
);

  wire [31:0] adder_1_out, adder_2_out, ext_1_extres, multiplexer_1_out, PC_q, shifter_1_out;

  Multiplexer #(.width(32)) multiplexer_1 (
    .in0(adder_1_out), .in1(adder_2_out), .out(multiplexer_1_out), .sel(PCSrc));  // open: en
  Register #(.width(32)) PC (.D(multiplexer_1_out), .Q(PC_q), .clk(Clk), .clr(Reset));  // open: en
  Adder #(.width(32)) adder_1 (.a(PC_q), .b(32'h1), .out(adder_1_out));  // open: cin, cout
  ROM #(.addrWidth(5), .dataWidth(32)) rom_1 (.addr(PC_q[4:0]), .data(Inst));  // open: sel
  EXT ext_1 (.Imm(Imm), .ExtOp(1'b1), .ExtRes(ext_1_extres));
  Shifter #(.width(32)) shifter_1 (.in(ext_1_extres), .\dist ({5{1'b0}}), .out(shifter_1_out));
  Adder #(.width(32)) adder_2 (.a(adder_1_out), .b(shifter_1_out), .out(adder_2_out));  // open: cin, cout

  // Notes on the sheet:
  //   contents of rom_1 (hex, n*v repeats v):
  //   34110020 34120000 34100000 12110009 8e48fffc 34090001 1094021 ae480000 34080004 2489021 34080001
  //   2088021 1000fff6
endmodule

module Controlller (
  input  [5:0] Op,
  input  [5:0] Funct,
  output MemtoReg,
  output MemWrite,
  output Branch,
  output [3:0] BranchOp,
  output [3:0] ALUCtrl,
  output ALUSrc,
  output RegDst,
  output RegWrite,
  output Extend
);

  wire addu, beq, lui, lw, not_1_out, not_2_out, not_3_out, not_4_out, not_5_out, not_6_out, not_7_out,
       not_8_out, not_9_out, not_10_out, not_11_out, not_12_out, or_8_out, or_9_out, or_10_out, or_11_out,
       or_12_out, ori, R, subu, sw;
  wire [3:0] multiplexer_1_out, multiplexer_2_out, multiplexer_3_out;

  not not_1 (not_1_out, Op[5]);
  buf or_1 (MemtoReg, lw);  // OR_Gate
  not not_2 (not_2_out, Op[3]);
  not not_3 (not_3_out, Op[4]);
  not not_4 (not_4_out, Op[2]);
  buf or_2 (MemWrite, sw);  // OR_Gate
  not not_5 (not_5_out, Op[0]);
  not not_6 (not_6_out, Op[1]);
  and u_R (R, not_1_out, not_3_out, not_2_out, not_4_out, not_6_out, not_5_out);
  and u_ori (ori, not_1_out, not_3_out, Op[3], Op[2], not_6_out, Op[0]);
  and u_lw (lw, Op[5], not_3_out, not_2_out, not_4_out, Op[1], Op[0]);
  and u_sw (sw, Op[5], not_3_out, Op[3], not_4_out, Op[1], Op[0]);
  and u_beq (beq, not_1_out, not_3_out, not_2_out, Op[2], not_6_out, not_5_out);
  and u_lui (lui, not_1_out, not_3_out, Op[3], Op[2], Op[1], Op[0]);
  buf or_3 (Branch, beq);  // OR_Gate
  or or_4 (ALUSrc, ori, lw, sw, lui);
  not not_7 (not_7_out, Funct[4]);
  not not_8 (not_8_out, Funct[5]);
  or or_5 (RegDst, addu, subu);
  not not_9 (not_9_out, Funct[3]);
  not not_10 (not_10_out, Funct[2]);
  or or_6 (RegWrite, addu, subu, ori, lw, lui);
  not not_11 (not_11_out, Funct[1]);
  not not_12 (not_12_out, Funct[0]);
  or or_7 (Extend, lw, sw, beq, lui);
  and R_2 (addu, Funct[5], not_7_out, not_9_out, not_10_out, not_11_out, Funct[0], R);
  and R_3 (subu, Funct[5], not_7_out, not_9_out, not_10_out, Funct[1], Funct[0], R);
  Multiplexer #(.width(4)) multiplexer_1 (
    .in0(4'b0000), .in1(4'b0111), .out(multiplexer_1_out), .sel(or_8_out));  // open: en
  buf or_8 (or_8_out, lui);  // OR_Gate
  buf or_9 (or_9_out, ori);  // OR_Gate
  Multiplexer #(.width(4)) multiplexer_2 (
    .in0(multiplexer_1_out), .in1(4'b0011), .out(multiplexer_2_out), .sel(or_9_out));  // open: en
  Multiplexer #(.width(4)) multiplexer_3 (
    .in0(multiplexer_2_out), .in1(4'b0001), .out(multiplexer_3_out), .sel(or_10_out));  // open: en
  buf or_10 (or_10_out, subu);  // OR_Gate
  Multiplexer #(.width(4)) multiplexer_4 (
    .in0(multiplexer_3_out), .in1(4'b0000), .out(ALUCtrl), .sel(or_11_out));  // open: en
  or or_11 (or_11_out, lw, addu, sw);
  Multiplexer #(.width(4)) multiplexer_5 (.in0(4'b0000), .in1(4'b0000), .out(BranchOp), .sel(or_12_out));  // open: en
  buf or_12 (or_12_out, beq);  // OR_Gate

  // Other names for the same wires on the sheet: f0 = Funct[0]; f1 = Funct[1]; f2 = Funct[2]; f3 = Funct[3];
  //   f4 = Funct[4]; f5 = Funct[5]
endmodule

module Inst_Pipeline (
  input  [31:0] in_1,
  output [5:0] Op,
  output [5:0] Funct,
  output [4:0] rs,
  output [4:0] rt,
  output [4:0] rd,
  output [15:0] imm,
  output [25:0] jumpaddress,
  output [4:0] rd_2
);


  assign Funct = in_1[5:0];
  assign imm = in_1[15:0];
  assign jumpaddress = in_1[25:0];
  assign Op = in_1[31:26];
  assign rd = in_1[15:11];
  assign rd_2 = in_1[10:6];
  assign rs = in_1[25:21];
  assign rt = in_1[20:16];
endmodule

module Branch (
  input  Branch,
  input  [3:0] BranchOp,
  input  [31:0] SrcA,
  input  [31:0] SrcB,
  output out_5
);

  wire and_1_out, beq, demultiplexer_1_out0, Res;

  Comparator #(.width(32), .mode("unsigned")) comparator_1 (.a(SrcA), .b(SrcB), .eq(beq));  // open: gt, lt
  Demultiplexer #(.select(4)) demultiplexer_1 (
    .out0(demultiplexer_1_out0), .in(1'b1), .sel(BranchOp));  // open: out1, out2, out3, out4, out5, out6, out7, out8, out9, out10, out11, out12, out13, out14, out15, en
  and and_1 (and_1_out, beq, demultiplexer_1_out0);
  buf or_1 (Res, and_1_out);  // OR_Gate
  and and_2 (out_5, Branch, Res);
endmodule

module CPU (
  input  Reset,
  output [31:0] out_2,
  output out_3,
  output [4:0] out_4,
  output [31:0] out_5,
  output out_6,
  output [4:0] out_7,
  output [31:0] out_8
);

  wire branch_1_out_5, Clk, controlller_1_alusrc, controlller_1_branch, controlller_1_extend,
       controlller_1_memtoreg, controlller_1_regdst;
  wire [3:0] controlller_1_aluctrl, controlller_1_branchop;
  wire [4:0] inst_pipeline_1_rd, inst_pipeline_1_rs, inst_pipeline_1_rt;
  wire [5:0] inst_pipeline_1_funct, inst_pipeline_1_op;
  wire [15:0] inst_pipeline_1_imm;
  wire [31:0] alu_1_alures, dm_1_rd, ext_1_extres, grf_1_out_8, multiplexer_2_out;

  Clock clock_1 (.out(Clk));
  // Probe on out_2
  Inst_Pipeline inst_pipeline_1 (
    .in_1(out_2), .Op(inst_pipeline_1_op), .Funct(inst_pipeline_1_funct), .rs(inst_pipeline_1_rs),
    .rt(inst_pipeline_1_rt), .rd(inst_pipeline_1_rd), .imm(inst_pipeline_1_imm));  // open: jumpaddress, rd_2
  IFU ifu_1 (.Imm(inst_pipeline_1_imm), .Inst(out_2), .PCSrc(branch_1_out_5), .Clk(Clk), .Reset(Reset));
  Controlller controlller_1 (
    .Op(inst_pipeline_1_op), .Funct(inst_pipeline_1_funct), .MemtoReg(controlller_1_memtoreg),
    .MemWrite(out_6), .Branch(controlller_1_branch), .BranchOp(controlller_1_branchop),
    .ALUCtrl(controlller_1_aluctrl), .ALUSrc(controlller_1_alusrc), .RegDst(controlller_1_regdst),
    .RegWrite(out_3), .Extend(controlller_1_extend));
  // Probe on out_4
  GRF grf_1 (
    .A1(inst_pipeline_1_rs), .A2(inst_pipeline_1_rt), .A3(out_4), .WD(out_5), .out_8(grf_1_out_8),
    .out_9(out_8), .clk(Clk), .reset(Reset), .WE(out_3));
  EXT ext_1 (.Imm(inst_pipeline_1_imm), .ExtOp(controlller_1_extend), .ExtRes(ext_1_extres));
  Multiplexer #(.width(5)) multiplexer_1 (
    .in0(inst_pipeline_1_rt), .in1(inst_pipeline_1_rd), .out(out_4), .sel(controlller_1_regdst));  // open: en
  Multiplexer #(.width(32)) multiplexer_2 (
    .in0(out_8), .in1(ext_1_extres), .out(multiplexer_2_out), .sel(controlller_1_alusrc));  // open: en
  ALU alu_1 (
    .SrcA(grf_1_out_8), .SrcB(multiplexer_2_out), .ALURes(alu_1_alures), .ALUCtrl(controlller_1_aluctrl));  // open: Zero
  Branch branch_1 (
    .SrcA(grf_1_out_8), .SrcB(multiplexer_2_out), .Branch(controlller_1_branch),
    .BranchOp(controlller_1_branchop), .out_5(branch_1_out_5));
  DM dm_1 (.Addr(alu_1_alures), .Data(out_8), .RD(dm_1_rd), .WE(out_6), .Reset(Reset), .out_7(out_7), .Clk(Clk));
  Multiplexer #(.width(32)) multiplexer_3 (
    .in0(alu_1_alures), .in1(dm_1_rd), .out(out_5), .sel(controlller_1_memtoreg));  // open: en

  // Other names for the same wires on the sheet: Inst[31:0] = out_2; MemAddr[4:0] = out_7; MemData[31:0] = out_8;
  //   MemWrite = out_6; RegAddr[4:0] = out_4; RegData[31:0] = out_5; RegWrite = out_3
endmodule

module testbench (
  input  in_1,
  output [31:0] out_2,
  output out_3,
  output [4:0] out_4,
  output [31:0] out_5,
  output out_6,
  output [4:0] out_7,
  output [31:0] out_8
);

  wire clock_1_out, comparator_1_gt;
  wire [7:0] counter_1_q;

  Clock clock_1 (.out(clock_1_out));
  Counter counter_1 (.Q(counter_1_q), .carry(in_1), .clk(clock_1_out));  // open: load, D, count, clr
  Comparator comparator_1 (.a(8'h4), .b(counter_1_q), .gt(comparator_1_gt));  // open: eq, lt
  main main_1 (
    .in_1(comparator_1_gt), .out_2(out_2), .out_3(out_3), .out_4(out_4), .out_5(out_5), .out_6(out_6),
    .out_7(out_7), .out_8(out_8));
  // Probe on out_2
endmodule
