// Logisim project CPU-wjk.circ as structural Verilog: 9 circuits, main circuit main
module main (
  input  in_1,
  output [31:0] out_2,
  output out_3,
  output [4:0] out_4,
  output [31:0] out_5,
  output out_6,
  output [4:0] out_7,
  output [31:0] out_8
);

  wire alu_1_zero, ALUScr, Branch, clk, MemRead, PCSrc, RegDst;
  wire [1:0] ALUOp, ExtCtrl, MemtoReg;
  wire [3:0] alucontroller_1_out_3;
  wire [31:0] alu_1_result, dm_1_rd, grf_1_rd1, multiplexer_2_out;
  wire [31:2] beq;
  wire [31:30] extern_1_out_3;

  Clock clock_1 (.out(clk));
  // Probe on out_2
  IFU ifu_1 (.PCSrc(PCSrc), .in_1({beq, 2'b00}), .reset(in_1), .instruction(out_2), .clk(clk));
  Controller controller_1 (
    .Op(out_2[31:26]), .RegDst(RegDst), .RegWrite(out_3), .ALUScr(ALUScr), .ExtCtrl(ExtCtrl),
    .MemRead(MemRead), .MemWrite(out_6), .Branch(Branch), .ALUOp(ALUOp), .MemtoReg(MemtoReg));
  Multiplexer #(.width(5), .enable("false")) multiplexer_1 (
    .in0(out_2[20:16]), .in1(out_2[15:11]), .out(out_4), .sel(RegDst));
  \extern  extern_1 (.in_1(out_2[15:0]), .ExtCtrl(ExtCtrl), .out_3({extern_1_out_3, beq}));
  GRF grf_1 (
    .RA1(out_2[25:21]), .RA2(out_2[20:16]), .WA(out_4), .WD(out_5), .RD1(grf_1_rd1), .RD2(out_8), .CLK(clk),
    .Reset(in_1), .WE(out_3));
  Multiplexer #(.width(32), .enable("false")) multiplexer_2 (
    .in0(out_8), .in1({extern_1_out_3, beq}), .out(multiplexer_2_out), .sel(ALUScr));
  ALUController alucontroller_1 (.Func(out_2[5:0]), .in_2(ALUOp), .out_3(alucontroller_1_out_3));
  and and_1 (PCSrc, Branch, alu_1_zero);
  ALU alu_1 (
    .A(grf_1_rd1), .B(multiplexer_2_out), .ALUCtrl(alucontroller_1_out_3), .zero(alu_1_zero),
    .result({alu_1_result[31:7], out_7, alu_1_result[1:0]}));
  DM dm_1 (
    .A({alu_1_result[31:7], out_7, alu_1_result[1:0]}), .WD(out_8), .WE(out_6), .clk(clk), .rst(in_1),
    .RD(dm_1_rd), .RE(MemRead));
  Multiplexer #(.select(2), .width(32), .enable("false")) multiplexer_3 (
    .in0({alu_1_result[31:7], out_7, alu_1_result[1:0]}), .in1(dm_1_rd), .in2({extern_1_out_3, beq}),
    .out(out_5), .sel(MemtoReg));  // open: in3

  // Other names for the same wires on the sheet: MemAddr[4:0] = out_7; Instr[31:0] = out_2; MemData[31:0] = out_8;
  //   MemWrite = out_6; RegAddr[4:0] = out_4; RegData[31:0] = out_5; RegWrite = out_3; rst = in_1
endmodule

module GRF (
  input  CLK,
  input  Reset,
  input  WE,
  input  [4:0] RA1,
  input  [4:0] RA2,
  input  [4:0] WA,
  input  [31:0] WD,
  output [31:0] RD1,
  output [31:0] RD2
);

  wire en1, en2, en3, en4, en5, en6, en7, en8, en9, en10, en11, en12, en13, en14, en15, en16, en17, en18,
       en19, en20, en21, en22, en23, en24, en25, en26, en27, en28, en29, en30, en31;
  wire [31:0] _0, _1, _2, _3, _4, _5, _6, _7, _8, _9, _10, _11, _12, _13, _14, _15, _16, _17, _18, _19, _20,
       _21, _22, _23, _24, _25, _26, _27, _28, _29, _30, _31;

  Multiplexer #(.select(5), .width(32), .enable("false")) multiplexer_1 (
    .in0(_0), .in1(_1), .in2(_2), .in3(_3), .in4(_4), .in5(_5), .in6(_6), .in7(_7), .in8(_8), .in9(_9),
    .in10(_10), .in11(_11), .in12(_12), .in13(_13), .in14(_14), .in15(_15), .in16(_16), .in17(_17),
    .in18(_18), .in19(_19), .in20(_20), .in21(_21), .in22(_22), .in23(_23), .in24(_24), .in25(_25),
    .in26(_26), .in27(_27), .in28(_28), .in29(_29), .in30(_30), .in31(_31), .out(RD1), .sel(RA1));
  Multiplexer #(.select(5), .width(32), .enable("false")) multiplexer_2 (
    .in0(_0), .in1(_1), .in2(_2), .in3(_3), .in4(_4), .in5(_5), .in6(_6), .in7(_7), .in8(_8), .in9(_9),
    .in10(_10), .in11(_11), .in12(_12), .in13(_13), .in14(_14), .in15(_15), .in16(_16), .in17(_17),
    .in18(_18), .in19(_19), .in20(_20), .in21(_21), .in22(_22), .in23(_23), .in24(_24), .in25(_25),
    .in26(_26), .in27(_27), .in28(_28), .in29(_29), .in30(_30), .in31(_31), .out(RD2), .sel(RA2));
  Register #(.width(32)) register_1 (.D({32{1'b0}}), .Q(_0), .clk(CLK), .clr(Reset));  // open: en
  Register #(.width(32)) register_2 (.D(WD), .en(en4), .Q(_4), .clk(CLK), .clr(Reset));
  Register #(.width(32)) register_3 (.D(WD), .en(en8), .Q(_8), .clk(CLK), .clr(Reset));
  Register #(.width(32)) register_4 (.D(WD), .en(en12), .Q(_12), .clk(CLK), .clr(Reset));
  Register #(.width(32)) register_5 (.D(WD), .en(en16), .Q(_16), .clk(CLK), .clr(Reset));
  Register #(.width(32)) register_6 (.D(WD), .en(en20), .Q(_20), .clk(CLK), .clr(Reset));
  Register #(.width(32)) register_7 (.D(WD), .en(en24), .Q(_24), .clk(CLK), .clr(Reset));
  Register #(.width(32)) register_8 (.D(WD), .en(en28), .Q(_28), .clk(CLK), .clr(Reset));
  Decoder #(.select(5), .disabled(0)) decoder_1 (
    .out1(en1), .out2(en2), .out3(en3), .out4(en4), .out5(en5), .out6(en6), .out7(en7), .out8(en8),
    .out9(en9), .out10(en10), .out11(en11), .out12(en12), .out13(en13), .out14(en14), .out15(en15),
    .out16(en16), .out17(en17), .out18(en18), .out19(en19), .out20(en20), .out21(en21), .out22(en22),
    .out23(en23), .out24(en24), .out25(en25), .out26(en26), .out27(en27), .out28(en28), .out29(en29),
    .out30(en30), .out31(en31), .sel(WA), .en(WE));  // open: out0
  Register #(.width(32)) register_9 (.D(WD), .en(en1), .Q(_1), .clk(CLK), .clr(Reset));
  Register #(.width(32)) register_10 (.D(WD), .en(en5), .Q(_5), .clk(CLK), .clr(Reset));
  Register #(.width(32)) register_11 (.D(WD), .en(en9), .Q(_9), .clk(CLK), .clr(Reset));
  Register #(.width(32)) register_12 (.D(WD), .en(en13), .Q(_13), .clk(CLK), .clr(Reset));
  Register #(.width(32)) register_13 (.D(WD), .en(en17), .Q(_17), .clk(CLK), .clr(Reset));
  Register #(.width(32)) register_14 (.D(WD), .en(en21), .Q(_21), .clk(CLK), .clr(Reset));
  Register #(.width(32)) register_15 (.D(WD), .en(en25), .Q(_25), .clk(CLK), .clr(Reset));
  Register #(.width(32)) register_16 (.D(WD), .en(en29), .Q(_29), .clk(CLK), .clr(Reset));
  Register #(.width(32)) register_17 (.D(WD), .en(en2), .Q(_2), .clk(CLK), .clr(Reset));
  Register #(.width(32)) register_18 (.D(WD), .en(en6), .Q(_6), .clk(CLK), .clr(Reset));
  Register #(.width(32)) register_19 (.D(WD), .en(en10), .Q(_10), .clk(CLK), .clr(Reset));
  Register #(.width(32)) register_20 (.D(WD), .en(en14), .Q(_14), .clk(CLK), .clr(Reset));
  Register #(.width(32)) register_21 (.D(WD), .en(en18), .Q(_18), .clk(CLK), .clr(Reset));
  Register #(.width(32)) register_22 (.D(WD), .en(en22), .Q(_22), .clk(CLK), .clr(Reset));
  Register #(.width(32)) register_23 (.D(WD), .en(en26), .Q(_26), .clk(CLK), .clr(Reset));
  Register #(.width(32)) register_24 (.D(WD), .en(en30), .Q(_30), .clk(CLK), .clr(Reset));
  Register #(.width(32)) register_25 (.D(WD), .en(en3), .Q(_3), .clk(CLK), .clr(Reset));
  Register #(.width(32)) register_26 (.D(WD), .en(en7), .Q(_7), .clk(CLK), .clr(Reset));
  Register #(.width(32)) register_27 (.D(WD), .en(en11), .Q(_11), .clk(CLK), .clr(Reset));
  Register #(.width(32)) register_28 (.D(WD), .en(en15), .Q(_15), .clk(CLK), .clr(Reset));
  Register #(.width(32)) register_29 (.D(WD), .en(en19), .Q(_19), .clk(CLK), .clr(Reset));
  Register #(.width(32)) register_30 (.D(WD), .en(en23), .Q(_23), .clk(CLK), .clr(Reset));
  Register #(.width(32)) register_31 (.D(WD), .en(en27), .Q(_27), .clk(CLK), .clr(Reset));
  Register #(.width(32)) register_32 (.D(WD), .en(en31), .Q(_31), .clk(CLK), .clr(Reset));

  // Other names for the same wires on the sheet: A1[4:0] = RA1; A2[4:0] = RA2; A3[4:0] = WA; rs = Reset
endmodule

module ALU (
  input  [3:0] ALUCtrl,
  input  [31:0] A,
  input  [31:0] B,
  output zero,
  output [31:0] result
);

  wire [31:0] _0, _1, _2, _3;

  Adder #(.width(32)) adder_1 (.a(A), .b(B), .out(_0));  // open: cin, cout
  Subtractor #(.width(32)) subtractor_1 (.a(A), .b(B), .out(_1));  // open: bin, bout
  assign _2 = A & B;  // AND_Gate and_1, 32 bits wide
  assign _3 = A | B;  // OR_Gate or_1, 32 bits wide
  Comparator #(.width(32), .mode("unsigned")) comparator_1 (.a(_1), .b({32{1'b0}}), .eq(zero));  // open: gt, lt
  Multiplexer #(.select(4), .width(32), .enable("false")) multiplexer_1 (
    .in0(_0), .in1(_1), .in2(_2), .in3(_3), .out(result), .sel(ALUCtrl));  // open: in4, in5, in6, in7, in8, in9, in10, in11, in12, in13, in14, in15
endmodule

module IFU (
  input  [31:0] in_1,
  input  PCSrc,
  input  clk,
  input  reset,
  output [31:0] instruction
);

  wire [31:0] adder_1_out, adder_2_out, multiplexer_1_out, register_1_q;

  Register #(.width(32)) register_1 (.D(multiplexer_1_out), .Q(register_1_q), .clk(clk), .clr(reset));  // open: en
  Adder #(.width(32)) adder_1 (.a(32'h4), .b(register_1_q), .out(adder_1_out));  // open: cin, cout
  Adder #(.width(32)) adder_2 (.a(adder_1_out), .b(in_1), .out(adder_2_out));  // open: cin, cout
  ROM #(.addrWidth(5), .dataWidth(32)) rom_1 (.addr(register_1_q[6:2]), .data(instruction));  // open: sel
  Multiplexer #(.width(32), .enable("false")) multiplexer_1 (
    .in0(adder_1_out), .in1(adder_2_out), .out(multiplexer_1_out), .sel(PCSrc));

  // Notes on the sheet:
  //   contents of rom_1 (hex, n*v repeats v):
  //   34110020 34120000 34100000 12110009 8e48fffc 34090001 1094021 ae480000 34080004 2489021 34080001
  //   2088021 1000fff6
endmodule

module DM (
  input  [31:0] A,
  input  [31:0] WD,
  input  RE,
  input  WE,
  input  clk,
  input  rst,
  output [31:0] RD
);

  RAM #(.addrWidth(5), .dataWidth(32), .bus("separate")) ram_1 (
    .addr(A[6:2]), .din(WD), .data(RD), .str(WE), .clk(clk), .ld(RE), .clr(rst));  // open: sel
endmodule

module \extern  (
  input  [15:0] in_1,
  input  [1:0] ExtCtrl,
  output [31:0] out_3
);

  wire [31:0] _0, _1, _2;

  assign _0 = {{16{1'b0}}, in_1};  // Bit_Extender bit_extender_1
  assign _1 = {{16{1'b1}}, in_1};  // Bit_Extender bit_extender_2
  assign _2 = {{16{in_1[15]}}, in_1};  // Bit_Extender bit_extender_3
  Multiplexer #(.select(2), .width(32), .enable("false")) multiplexer_1 (
    .in0(_0), .in1(_1), .in2(_2), .in3({in_1, {16{1'b0}}}), .out(out_3), .sel(ExtCtrl));

  // Other names for the same wires on the sheet: _3[31:16] = in_1; in[15:0] = in_1
endmodule

module Controller (
  input  [5:0] Op,
  output RegDst,
  output RegWrite,
  output ALUScr,
  output [1:0] ExtCtrl,
  output MemRead,
  output MemWrite,
  output [1:0] MemtoReg,
  output Branch,
  output [1:0] ALUOp
);

  wire and_2_out;

  and and_1 (RegDst, ~Op[5], ~Op[4], ~Op[3], ~Op[2], ~Op[1], ~Op[0]);  // AND_Gate
  and and_2 (and_2_out, ~Op[5], ~Op[4], Op[3], Op[2], ~Op[1], Op[0]);  // AND_Gate
  and and_3 (MemRead, Op[5], ~Op[4], ~Op[3], ~Op[2], Op[1], Op[0]);  // AND_Gate
  and and_4 (MemWrite, Op[5], ~Op[4], Op[3], ~Op[2], Op[1], Op[0]);  // AND_Gate
  and and_5 (Branch, ~Op[5], ~Op[4], ~Op[3], Op[2], ~Op[1], ~Op[0]);  // AND_Gate
  and and_6 (ALUOp[0], ~Op[5], ~Op[4], Op[3], Op[2], Op[1], Op[0]);  // AND_Gate
  or or_1 (RegWrite, RegDst, and_2_out, MemRead, ALUOp[0]);
  or or_2 (ALUScr, and_2_out, MemRead, MemWrite);
  or or_3 (ExtCtrl[1], MemRead, MemWrite, Branch, ALUOp[0]);
  or or_4 (ALUOp[1], RegDst, and_2_out);

  assign ExtCtrl[0] = ALUOp[0];
  assign MemtoReg = {ALUOp[0], MemRead};
endmodule

module ALUController (
  input  [5:0] Func,
  input  [1:0] in_2,
  output [3:0] out_3
);

  wire _00, _01, _10, _11, and_10_out, or_1_out, or_2_out, tunnel, tunnel_t, tunnel_t_t, tunnel_t_t_t;

  and and_1 (_00, ~in_2[1], ~in_2[0]);  // AND_Gate
  and and_2 (tunnel_t, Func[5], ~Func[4], ~Func[3], ~Func[2], ~Func[1], ~Func[0]);  // AND_Gate
  and and_3 (_01, ~in_2[1], in_2[0]);  // AND_Gate
  and and_4 (_10, in_2[1], ~in_2[0]);  // AND_Gate
  and and_5 (tunnel_t_t, Func[5], ~Func[4], ~Func[3], ~Func[2], Func[1], Func[0]);  // AND_Gate
  and and_6 (_11, in_2[1], in_2[0]);
  and and_7 (tunnel, Func[5], ~Func[4], ~Func[3], Func[2], ~Func[1], ~Func[0]);  // AND_Gate
  and and_8 (tunnel_t_t_t, Func[5], ~Func[4], ~Func[3], Func[2], ~Func[1], Func[0]);  // AND_Gate
  or or_1 (or_1_out, tunnel, tunnel_t_t_t);
  or or_2 (or_2_out, tunnel_t_t_t, tunnel_t_t);
  and and_9 (out_3[1], or_1_out, _10);
  and and_10 (and_10_out, or_2_out, _10);
  or or_3 (out_3[0], _01, and_10_out);

  assign out_3[3:2] = 2'b00;
endmodule

module CPU (
  input  in_1
);

  wire alu_1_zero, ALUScr, Branch, clk, MemRead, MemWrite, PCSrc, RegDst, RegWrite;
  wire [1:0] ALUOp, ExtCtrl, MemtoReg;
  wire [3:0] alucontroller_1_out_3;
  wire [4:0] multiplexer_1_out;
  wire [31:0] alu_1_result, dm_1_rd, grf_1_rd1, grf_1_rd2, ifu_1_instruction, multiplexer_2_out,
       multiplexer_3_out;
  wire [31:2] beq;
  wire [31:30] extern_1_out_3;

  Clock clock_1 (.out(clk));
  // Probe on ifu_1_instruction
  IFU ifu_1 (.PCSrc(PCSrc), .in_1({beq, 2'b00}), .reset(in_1), .instruction(ifu_1_instruction), .clk(clk));
  Controller controller_1 (
    .Op(ifu_1_instruction[31:26]), .RegDst(RegDst), .RegWrite(RegWrite), .ALUScr(ALUScr), .ExtCtrl(ExtCtrl),
    .MemRead(MemRead), .MemWrite(MemWrite), .Branch(Branch), .ALUOp(ALUOp), .MemtoReg(MemtoReg));
  Multiplexer #(.width(5), .enable("false")) multiplexer_1 (
    .in0(ifu_1_instruction[20:16]), .in1(ifu_1_instruction[15:11]), .out(multiplexer_1_out), .sel(RegDst));
  \extern  extern_1 (.in_1(ifu_1_instruction[15:0]), .ExtCtrl(ExtCtrl), .out_3({extern_1_out_3, beq}));
  GRF grf_1 (
    .RA1(ifu_1_instruction[25:21]), .RA2(ifu_1_instruction[20:16]), .WA(multiplexer_1_out),
    .WD(multiplexer_3_out), .RD1(grf_1_rd1), .RD2(grf_1_rd2), .CLK(clk), .Reset(in_1), .WE(RegWrite));
  ALUController alucontroller_1 (.Func(ifu_1_instruction[5:0]), .in_2(ALUOp), .out_3(alucontroller_1_out_3));
  Multiplexer #(.width(32), .enable("false")) multiplexer_2 (
    .in0(grf_1_rd2), .in1({extern_1_out_3, beq}), .out(multiplexer_2_out), .sel(ALUScr));
  and and_1 (PCSrc, Branch, alu_1_zero);
  ALU alu_1 (
    .A(grf_1_rd1), .B(multiplexer_2_out), .ALUCtrl(alucontroller_1_out_3), .zero(alu_1_zero),
    .result(alu_1_result));
  DM dm_1 (.A(alu_1_result), .WD(grf_1_rd2), .WE(MemWrite), .clk(clk), .rst(in_1), .RD(dm_1_rd), .RE(MemRead));
  Multiplexer #(.select(2), .width(32), .enable("false")) multiplexer_3 (
    .in0(alu_1_result), .in1(dm_1_rd), .in2({extern_1_out_3, beq}), .out(multiplexer_3_out), .sel(MemtoReg));  // open: in3

  // Other names for the same wires on the sheet: rst = in_1
endmodule
